# Fritzing sketch demo_02_reading_LDR (saved by Fritzing 1.0.6)
breadboards: 1

parts:
  A1 = Esp32-c3 super mini
  LED1 = LED - 5mm [color="Red (633nm)" current=0.030A package="5 mm [THT]"]
  R1 = Resistor [tolerance=±5% power=0.25W resistance=220 package=THT]

nets:
  N1: A1.Pin_8, R1.Pin_0
  N2: A1.Pin_15, LED1.cathode
  N3: LED1.anode, R1.Pin_1

custom parts:
  Esp32-c3 super mini: ESP32-C3 Development Board ESP32 SuperMini Development Board ESP32 Development Board WiFi Bluetooth.
