# Fritzing sketch demo_03_HCSR04 (saved by Fritzing 1.0.6)
breadboards: 1

parts:
  A1 = Esp32-c3 super mini
  HC-SR04_Sensor_2 = HC-SR04 Ultrasonic Distance Sensor

nets:
  N1: A1.Pin_7, HC-SR04_Sensor_2.TRIG
  N2: A1.Pin_8, HC-SR04_Sensor_2.ECHO
  N3: A1.Pin_14, HC-SR04_Sensor_2.VCC
  N4: A1.Pin_15, HC-SR04_Sensor_2.GND

custom parts:
  Esp32-c3 super mini: ESP32-C3 Development Board ESP32 SuperMini Development Board ESP32 Development Board WiFi Bluetooth.
  HC-SR04 Ultrasonic Distance Sensor: The HC-SR04 is an ultrasonic distance sensor. It is capable of providing measurement for ranges of 2cm to 400cm. The module operates at 5V.
