# Fritzing sketch demo_04_BMP280 (saved by Fritzing 1.0.6)
breadboards: 1

parts:
  M1 = BME280
  A1 = Esp32-c3 super mini

nets (from the schematic view):
  N1: M1.VIN, A1.Pin_14
  N2: M1.GND, A1.Pin_15
  N3: M1.SCL, A1.Pin_4
  N4: M1.SDA, A1.Pin_5

custom parts:
  BME280: Temperature Humidity Barometric presure Sensor
  Esp32-c3 super mini: ESP32-C3 Development Board ESP32 SuperMini Development Board ESP32 Development Board WiFi Bluetooth.
