# Fritzing sketch 091_oled (saved by Fritzing 1.0.6)
breadboards: 1

parts:
  A1 = Esp32-c3 super mini
  S1 = 0.91 inch OLED I2C Display 128 x 32 Pixels

nets:
  N1: A1.Pin_4, S1.SCL
  N2: A1.Pin_5, S1.SDA
  N3: A1.Pin_14, S1.VCC
  N4: A1.Pin_15, S1.GND

custom parts:
  Esp32-c3 super mini: ESP32-C3 Development Board ESP32 SuperMini Development Board ESP32 Development Board WiFi Bluetooth.
