# Fritzing sketch dht22 (saved by Fritzing 1.0.6)
breadboards: 1

parts:
  A1 = Esp32-c3 super mini
  A2 = DHT22 module

nets:
  N1: A1.Pin_8, A2.Out
  N2: A1.Pin_14, A2.+
  N3: A1.Pin_15, A2.-

custom parts:
  Esp32-c3 super mini: ESP32-C3 Development Board ESP32 SuperMini Development Board ESP32 Development Board WiFi Bluetooth.
  DHT22 module: DHT22 module. Pins VCC Data GND.
